// Logisim project 32 Bit FPU.circ as structural Verilog: 5 circuits, main circuit main
module main (
  input  [1:0] control,
  input  [31:0] Input1,
  input  [31:0] Input2,
  output [31:0] Output,
  output Addition__Subtraction_Multiplication_Overflow__Divide_by_0_indicator
);

  wire Adder_overflow, Divider_divide_by_zero, Multiplier_overflow, Subtractor_overflow;
  wire [31:0] Adder_output, Divider_output, Multiplier_output, Subtractor_output;

  // Probe on Input1
  // Probe on Input2
  FPU_Adder Adder (.A(Input1), .B(Input2), .Output(Adder_output), .Overflow(Adder_overflow));
  FPU_Subtractor Subtractor (.A(Input1), .B(Input2), .Output(Subtractor_output), .Overflow(Subtractor_overflow));
  FPU_Multiplier Multiplier (.A(Input1), .B(Input2), .Output(Multiplier_output), .Overflow(Multiplier_overflow));
  FPU_divider Divider (.A(Input1), .B(Input2), .Output(Divider_output), .Divide_by_Zero(Divider_divide_by_zero));
  Multiplexer #(.select(2), .width(32), .enable("false")) multiplexer_1 (
    .in0(Adder_output), .in1(Subtractor_output), .in2(Multiplier_output), .in3(Divider_output), .out(Output),
    .sel(control));
  Multiplexer #(.select(2), .enable("false")) multiplexer_2 (
    .in0(Adder_overflow), .in1(Subtractor_overflow), .in2(Multiplier_overflow), .in3(Divider_divide_by_zero),
    .out(Addition__Subtraction_Multiplication_Overflow__Divide_by_0_indicator), .sel(control));
  // Probe on Output

  // Notes on the sheet:
  //   32 BIT FPU
  //   Divya Prakash
  //   National Institute of Technology Patna
  //   00: Addition
  //   01: Subtraction
  //   10: Multiplication
  //   11: Division
  //   Flags
endmodule

module FPU_Adder (
  input  [31:0] A,
  input  [31:0] B,
  output [31:0] Output,
  output Overflow
);

  wire adder_3_cout, comparator_1_gt, comparator_2_eq, comparator_3_gt, multiplexer_3_out;
  wire [7:0] adder_1_out, adder_2_out, multiplexer_1_out, multiplexer_2_out, subtractor_1_out,
       subtractor_2_out, subtractor_3_out;

  // Probe on A
  // Probe on B
  xor xor_1 (Output[31], B[31], A[31]);
  Comparator comparator_1 (.a(A[30:23]), .b(B[30:23]), .gt(comparator_1_gt));  // open: eq, lt
  Adder adder_1 (.a(A[30:23]), .b(8'h1), .out(adder_1_out));  // open: cin, cout
  Adder adder_2 (.a(B[30:23]), .b(8'h1), .out(adder_2_out));  // open: cin, cout
  Adder #(.width(23)) adder_3 (.a(A[22:0]), .b(B[22:0]), .out(Output[22:0]), .cout(adder_3_cout));  // open: cin
  Multiplexer #(.width(8), .enable("false")) multiplexer_1 (
    .in0(adder_1_out), .in1(adder_2_out), .out(multiplexer_1_out), .sel(comparator_1_gt));
  Multiplexer #(.width(8), .enable("false")) multiplexer_2 (
    .in0(A[30:23]), .in1(B[30:23]), .out(multiplexer_2_out), .sel(comparator_1_gt));
  Comparator #(.width(1)) comparator_2 (.a(adder_3_cout), .b(1'b0), .eq(comparator_2_eq));  // open: gt, lt
  Subtractor subtractor_1 (.a(B[30:23]), .b(A[30:23]), .out(subtractor_1_out));  // open: bin, bout
  Comparator comparator_3 (.a(multiplexer_1_out), .b({8{1'b1}}), .gt(comparator_3_gt));  // open: eq, lt
  Subtractor subtractor_2 (.a({8{1'b0}}), .b(subtractor_1_out), .out(subtractor_2_out));  // open: bin, bout
  Multiplexer #(.enable("false")) multiplexer_3 (
    .in0(1'b1), .in1(1'b0), .out(multiplexer_3_out), .sel(comparator_3_gt));
  Subtractor subtractor_3 (.a(multiplexer_2_out), .b(subtractor_2_out), .out(subtractor_3_out));  // open: bin, bout
  Multiplexer #(.width(8), .enable("false")) multiplexer_4 (
    .in0(multiplexer_1_out), .in1(subtractor_3_out), .out(Output[30:23]), .sel(comparator_2_eq));
  and and_1 (Overflow, multiplexer_3_out, Output[31]);
  // Probe on Output
endmodule

module FPU_Subtractor (
  input  [31:0] A,
  input  [31:0] B,
  output [31:0] Output,
  output Overflow
);

  wire comparator_1_gt, comparator_2_eq, comparator_3_lt, multiplexer_3_out, subtractor_1_bout;
  wire [7:0] adder_1_out, adder_2_out, adder_3_out, multiplexer_1_out, multiplexer_2_out, subtractor_2_out,
       subtractor_3_out;

  // Probe on A
  // Probe on B
  xor xor_1 (Output[31], B[31], A[31]);
  Comparator comparator_1 (.a(A[30:23]), .b(B[30:23]), .gt(comparator_1_gt));  // open: eq, lt
  Adder adder_1 (.a(A[30:23]), .b(8'h1), .out(adder_1_out));  // open: cin, cout
  Adder adder_2 (.a(B[30:23]), .b(8'h1), .out(adder_2_out));  // open: cin, cout
  Subtractor #(.width(23)) subtractor_1 (
    .a(A[22:0]), .b(B[22:0]), .out(Output[22:0]), .bout(subtractor_1_bout));  // open: bin
  Multiplexer #(.width(8), .enable("false")) multiplexer_1 (
    .in0(adder_1_out), .in1(adder_2_out), .out(multiplexer_1_out), .sel(comparator_1_gt));
  Multiplexer #(.width(8), .enable("false")) multiplexer_2 (
    .in0(A[30:23]), .in1(B[30:23]), .out(multiplexer_2_out), .sel(comparator_1_gt));
  Comparator #(.width(1)) comparator_2 (.a(subtractor_1_bout), .b(1'b0), .eq(comparator_2_eq));  // open: gt, lt
  Subtractor subtractor_2 (.a(B[30:23]), .b(A[30:23]), .out(subtractor_2_out));  // open: bin, bout
  Comparator comparator_3 (.a(multiplexer_2_out), .b({8{1'b0}}), .lt(comparator_3_lt));  // open: gt, eq
  Subtractor subtractor_3 (.a({8{1'b0}}), .b(subtractor_2_out), .out(subtractor_3_out));  // open: bin, bout
  Multiplexer #(.enable("false")) multiplexer_3 (
    .in0(1'b1), .in1(1'b0), .out(multiplexer_3_out), .sel(comparator_3_lt));
  Adder adder_3 (.a(multiplexer_2_out), .b(subtractor_3_out), .out(adder_3_out));  // open: cin, cout
  and and_1 (Overflow, multiplexer_3_out, Output[31]);
  Multiplexer #(.width(8), .enable("false")) multiplexer_4 (
    .in0(multiplexer_1_out), .in1(adder_3_out), .out(Output[30:23]), .sel(comparator_2_eq));
  // Probe on Output
endmodule

module FPU_Multiplier (
  input  [31:0] A,
  input  [31:0] B,
  output [31:0] Output,
  output Overflow
);

  wire comparator_1_eq;
  wire [7:0] adder_1_out;

  // Probe on A
  // Probe on B
  xor xor_1 (Output[31], B[31], A[31]);
  Adder adder_1 (.a(A[30:23]), .b(B[30:23]), .out(adder_1_out));  // open: cin, cout
  Multiplier #(.width(23)) multiplier_1 (.a(A[22:0]), .b(B[22:0]), .out(Output[22:0]));  // open: cin, cout
  Subtractor subtractor_1 (.a(adder_1_out), .b(8'h7f), .out(Output[30:23]));  // open: bin, bout
  Comparator comparator_1 (.a(Output[30:23]), .b({8{1'b1}}), .eq(comparator_1_eq));  // open: gt, lt
  Multiplexer #(.enable("false")) multiplexer_1 (.in0(1'b0), .in1(1'b1), .out(Overflow), .sel(comparator_1_eq));
  // Probe on Output
endmodule

module FPU_divider (
  input  [31:0] A,
  input  [31:0] B,
  output [31:0] Output,
  output Divide_by_Zero
);

  wire comparator_1_eq;
  wire [7:0] subtractor_1_out, subtractor_2_out;

  // Probe on A
  // Probe on B
  xor xor_1 (Output[31], B[31], A[31]);
  Comparator comparator_1 (.a(B[30:23]), .b({8{1'b0}}), .eq(comparator_1_eq));  // open: gt, lt
  Subtractor subtractor_1 (.a(A[30:23]), .b(8'h7f), .out(subtractor_1_out));  // open: bin, bout
  Subtractor subtractor_2 (.a(B[30:23]), .b(8'h7f), .out(subtractor_2_out));  // open: bin, bout
  Divider #(.width(23)) divider_1 (.a(A[22:0]), .b(B[22:0]), .out(Output[22:0]));  // open: upper, rem
  Adder adder_1 (.a(subtractor_1_out), .b(subtractor_2_out), .out(Output[30:23]));  // open: cin, cout
  Multiplexer #(.enable("false")) multiplexer_1 (.in0(1'b0), .in1(1'b1), .out(Divide_by_Zero), .sel(comparator_1_eq));
  // Probe on Output

  // Notes on the sheet:
  //   Dividing Significands
  //   Adding Exponents
endmodule
